// Logisim project Proejct 1 (Circuit (NAND Only)).circ as structural Verilog: 1 circuit, main circuit main
module main (
  input  A,
  input  B,
  input  C,
  input  D,
  output R1,
  output G1
);

  wire nand_1_out, nand_2_out, nand_3_out, nand_4_out, nand_5_out, nand_6_out, nand_7_out, nand_8_out;

  nand nand_1 (nand_1_out, B, 1'b1);
  nand nand_2 (nand_2_out, C, 1'b1);
  nand nand_3 (nand_3_out, D, 1'b1);
  nand nand_4 (nand_4_out, nand_1_out, D);
  nand nand_5 (nand_5_out, nand_2_out, nand_3_out);
  nand nand_6 (nand_6_out, nand_1_out, C, D);
  nand nand_7 (nand_7_out, C, nand_4_out);
  nand nand_8 (nand_8_out, nand_2_out, D);
  nand nand_9 (G1, nand_5_out, nand_6_out);
  nand nand_10 (R1, nand_7_out, nand_8_out);
endmodule
