// Logisim project Project 1 (Bubble Push (R1)).circ as structural Verilog: 1 circuit, main circuit main
module main (
  input  A,
  input  B,
  input  C,
  input  D,
  input  in_5,
  input  in_6,
  input  in_7,
  input  in_8,
  output R1,
  output out_10
);

  wire and_1_out, and_2_out, nand_1_out, nand_2_out, nand_3_out, nand_4_out, nand_5_out, not_1_out,
       not_2_out, or_1_out;

  nand nand_1 (nand_1_out, in_6, 1'b1);
  nand nand_2 (nand_2_out, in_7, 1'b1);
  not not_1 (not_1_out, C);
  not not_2 (not_2_out, D);
  or or_1 (or_1_out, B, not_2_out);
  nand nand_3 (nand_3_out, nand_1_out, in_8);
  and and_1 (and_1_out, C, or_1_out);
  nand nand_4 (nand_4_out, in_7, nand_3_out);
  nand nand_5 (nand_5_out, nand_2_out, in_8);
  and and_2 (and_2_out, not_1_out, D);
  nand nand_6 (out_10, nand_4_out, nand_5_out);
  or or_2 (R1, and_1_out, and_2_out);
endmodule
