// Logisim project Project 1 (Circuit (Sum of Products)).circ as structural Verilog: 1 circuit, main circuit main
module main (
  input  A,
  input  B,
  input  C,
  input  D,
  output R1,
  output G1,
  output R2,
  output G2,
  output R3,
  output G3,
  output R4,
  output G4
);

  wire and_1_out, and_2_out, and_3_out, and_4_out, and_5_out, and_6_out, and_7_out, and_8_out, and_9_out,
       and_10_out, and_11_out, and_12_out, and_13_out, not_1_out, not_2_out, not_3_out, not_4_out, not_5_out,
       or_1_out, or_3_out;

  not not_1 (not_1_out, A);
  not not_2 (not_2_out, B);
  not not_3 (not_3_out, C);
  not not_4 (not_4_out, D);
  or or_1 (or_1_out, B, not_4_out);
  and and_1 (and_1_out, C, or_1_out);
  and and_2 (and_2_out, not_3_out, not_4_out);
  and and_3 (and_3_out, not_2_out, C, D);
  and and_4 (and_4_out, D, C);
  and and_5 (and_5_out, not_2_out, D);
  and and_6 (and_6_out, B, not_3_out);
  and and_7 (and_7_out, not_4_out, B);
  and and_8 (and_8_out, B, C, not_4_out);
  and and_9 (and_9_out, not_1_out, not_2_out, not_3_out, D);
  and and_10 (and_10_out, B, not_3_out);
  and and_11 (and_11_out, C, D);
  and and_12 (and_12_out, C, B);
  not not_5 (not_5_out, and_12_out);
  and and_13 (and_13_out, not_3_out, D);
  or or_2 (G1, and_2_out, and_3_out);
  or or_3 (or_3_out, and_4_out, and_5_out);
  or or_4 (G2, and_6_out, and_7_out);
  or or_5 (R3, and_8_out, and_9_out);
  or or_6 (G3, and_10_out, and_11_out);
  and and_14 (R4, D, not_5_out, not_1_out);
  or or_7 (R1, and_1_out, and_13_out);
  or or_8 (R2, A, or_3_out);

  assign G4 = 1'b0;
endmodule
