// Logisim project Project 2 (Circuit FIle).circ as structural Verilog: 1 circuit, main circuit main
module main (
  input  A,
  input  B,
  input  C,
  input  D
);

  wire and_1_out, and_2_out, and_3_out, and_4_out, and_5_out, and_6_out, and_7_out, and_8_out, and_10_out,
       and_11_out, and_12_out, and_13_out, and_14_out, and_15_out, and_16_out, and_17_out, and_18_out,
       and_19_out, clock_1_out, n7447_1_pin2, n7447_1_pin3, n7447_1_pin9, n7447_1_pin10, n7447_1_pin11,
       n7447_1_pin12, n7447_1_pin13, n7447_1_pin14, n7447_1_pin15, n7447_2_pin3, n7447_2_pin9, n7447_2_pin10,
       n7447_2_pin11, n7447_2_pin12, n7447_2_pin13, n7447_2_pin14, n7447_2_pin15, not_1_out, not_2_out,
       not_3_out, not_4_out, or_1_out, or_2_out, or_3_out, or_4_out, or_5_out, or_6_out, or_7_out, or_8_out,
       or_9_out, Q0_q, Q0_qn, Q1_q, Q1_qn, Q2_q, Q2_qn, xor_1_out;
  wire [1:1] and_9_out;
  wire [2:0] undriven, undriven_2;
  wire [3:0] undriven_3, undriven_4;

  not not_1 (not_1_out, A);
  not not_2 (not_2_out, B);
  xor xor_1 (xor_1_out, A, B);
  not not_3 (not_3_out, xor_1_out);
  and and_1 (and_1_out, B, Q0_q, not_1_out);
  and and_2 (and_2_out, A, not_2_out);
  or or_1 (or_1_out, and_1_out, and_2_out);
  and and_3 (and_3_out, A, not_2_out, Q0_q);
  and and_4 (and_4_out, not_1_out, Q0_qn);
  or or_2 (or_2_out, xor_1_out, Q0_q);
  and and_5 (and_5_out, Q2_qn, Q1_q);
  and and_6 (and_6_out, not_2_out, Q1_qn);
  and and_7 (and_7_out, and_5_out, or_1_out);
  or or_3 (or_3_out, not_3_out, and_4_out);
  or or_4 (or_4_out, not_3_out, and_6_out);
  or or_5 (or_5_out, Q1_q, or_2_out);
  and and_8 (and_8_out, Q2_qn, or_6_out);
  or or_6 (or_6_out, or_1_out, Q1_q);
  and and_9 (and_9_out[1], and_3_out, and_5_out);
  and and_10 (and_10_out, Q1_q, or_3_out);
  and and_11 (and_11_out, Q1_qn, or_1_out);
  and and_12 (and_12_out, and_4_out, B);
  and and_13 (and_13_out, Q0_q, or_4_out);
  and and_14 (and_14_out, Q2_qn, or_5_out);
  or or_7 (or_7_out, and_3_out, and_15_out);
  and and_15 (and_15_out, Q1_q, or_2_out);
  and and_16 (and_16_out, 1'b1, Q2_qn, or_8_out);
  or or_8 (or_8_out, and_10_out, and_11_out);
  and and_17 (and_17_out, Q2_qn, or_9_out);
  or or_9 (or_9_out, and_12_out, and_13_out);
  and and_18 (and_18_out, Q2_qn, or_7_out);
  Clock clock_1 (.out(clock_1_out));
  not not_4 (not_4_out, C);
  and and_19 (and_19_out, not_4_out, clock_1_out);
  _7447 #(.ShowInternalStructure("true")) u_7447_1 (
    .pin1(and_9_out[1]), .pin2(n7447_1_pin2), .pin3(n7447_1_pin3), .pin4(n7447_1_pin3), .pin5(n7447_1_pin3),
    .pin6(n7447_1_pin2), .pin7(n7447_1_pin2), .pin15(n7447_1_pin15), .pin14(n7447_1_pin14),
    .pin13(n7447_1_pin13), .pin12(n7447_1_pin12), .pin11(n7447_1_pin11), .pin10(n7447_1_pin10),
    .pin9(n7447_1_pin9));
  D_Flip_Flop Q2 (.D(and_7_out), .clk(and_19_out), .Q(Q2_q), .Qn(Q2_qn), .reset(D));  // open: preset
  D_Flip_Flop Q1 (.D(and_16_out), .clk(and_19_out), .Q(Q1_q), .Qn(Q1_qn), .reset(D));  // open: preset
  D_Flip_Flop Q0 (.D(and_17_out), .clk(and_19_out), .Q(Q0_q), .Qn(Q0_qn), .reset(D));  // open: preset
  LED R1 (.in(1'b1));
  LED G1 (.in(and_14_out));
  LED R2 (.in(and_8_out));
  LED G2 (.in(and_18_out));
  LED R3 (.in(and_7_out));
  // BCD_to_7_Segment_decoder bcd_to_7_segment_decoder_1: pin names not known; wires that end beside it: {2'b00, and_9_out[1], 1'b0}
  // BCD_to_7_Segment_decoder bcd_to_7_segment_decoder_2: pin names not known; wires that end beside it: {1'b0, and_9_out[1], 1'b0, and_9_out[1]}
  _7_Segment_Display #(.active("false"), .decimalPoint("false")) u_7_segment_display_1 (
    .g(n7447_1_pin14), .f(n7447_1_pin15), .a(n7447_1_pin13), .b(n7447_1_pin12), .e(n7447_1_pin9),
    .d(n7447_1_pin10), .c(n7447_1_pin11));
  _7_Segment_Display u_7_segment_display_2 (
    .g(undriven_3[3]), .f(undriven_3[2]), .a(undriven_3[1]), .b(undriven_3[0]), .e(undriven[2]),
    .d(undriven[1]), .c(undriven[0]));  // open: dp
  _7_Segment_Display u_7_segment_display_3 (
    .g(undriven_4[3]), .f(undriven_4[2]), .a(undriven_4[1]), .b(undriven_4[0]), .e(undriven_2[2]),
    .d(undriven_2[1]), .c(undriven_2[0]));  // open: dp
  _7447 #(.ShowInternalStructure("true")) u_7447_2 (
    .pin1(n7447_1_pin2), .pin2(and_9_out[1]), .pin3(n7447_2_pin3), .pin4(n7447_2_pin3), .pin5(n7447_2_pin3),
    .pin6(n7447_1_pin2), .pin7(and_9_out[1]), .pin15(n7447_2_pin15), .pin14(n7447_2_pin14),
    .pin13(n7447_2_pin13), .pin12(n7447_2_pin12), .pin11(n7447_2_pin11), .pin10(n7447_2_pin10),
    .pin9(n7447_2_pin9));
  _7_Segment_Display #(.active("false"), .decimalPoint("false")) u_7_segment_display_4 (
    .g(n7447_2_pin14), .f(n7447_2_pin15), .a(n7447_2_pin13), .b(n7447_2_pin12), .e(n7447_2_pin9),
    .d(n7447_2_pin10), .c(n7447_2_pin11));
  // also tied to GND on the sheet: n7447_1_pin2
  // also tied to VCC on the sheet: {n7447_1_pin3, n7447_2_pin3}

  // Notes on the sheet:
  //   q0
  //   q1
  //   q2
endmodule
