// Logisim project Project 3 (74HC157).circ as structural Verilog: 1 circuit, main circuit cmos_74HC157
module cmos_74HC157 (
  input  S,
  input  E,
  input  A1,
  input  A0,
  input  B1,
  input  B0,
  input  C1,
  input  C0,
  input  D1,
  input  D0,
  output Y1,
  output Y2,
  output Y3,
  output Y4
);

  wire and_1_out, and_2_out, and_3_out, and_4_out, and_5_out, and_6_out, and_7_out, and_8_out, buffer_1_out,
       buffer_2_out, buffer_3_out, buffer_4_out, buffer_5_out, buffer_6_out, buffer_7_out, buffer_8_out,
       buffer_9_out, buffer_10_out, nor_1_out, nor_2_out, nor_3_out, nor_4_out, nor_5_out, nor_6_out,
       not_1_out;

  buf buffer_1 (buffer_1_out, S);
  buf buffer_2 (buffer_2_out, E);
  buf buffer_3 (buffer_3_out, A1);
  buf buffer_4 (buffer_4_out, A0);
  buf buffer_5 (buffer_5_out, B1);
  buf buffer_6 (buffer_6_out, B0);
  buf buffer_7 (buffer_7_out, C1);
  buf buffer_8 (buffer_8_out, C0);
  buf buffer_9 (buffer_9_out, D1);
  buf buffer_10 (buffer_10_out, D0);
  not not_1 (not_1_out, buffer_1_out);
  nor nor_1 (nor_1_out, not_1_out, buffer_2_out);
  nor nor_2 (nor_2_out, buffer_1_out, buffer_2_out);
  and and_1 (and_1_out, nor_1_out, buffer_3_out);
  and and_2 (and_2_out, nor_2_out, buffer_4_out);
  and and_3 (and_3_out, nor_1_out, buffer_5_out);
  and and_4 (and_4_out, nor_2_out, buffer_6_out);
  and and_5 (and_5_out, nor_1_out, buffer_7_out);
  and and_6 (and_6_out, nor_2_out, buffer_8_out);
  and and_7 (and_7_out, nor_1_out, buffer_9_out);
  and and_8 (and_8_out, nor_2_out, buffer_10_out);
  nor nor_3 (nor_3_out, and_1_out, and_2_out);
  not not_2 (Y1, nor_3_out);
  nor nor_4 (nor_4_out, and_3_out, and_4_out);
  not not_3 (Y2, nor_4_out);
  nor nor_5 (nor_5_out, and_5_out, and_6_out);
  not not_4 (Y3, nor_5_out);
  nor nor_6 (nor_6_out, and_7_out, and_8_out);
  not not_5 (Y4, nor_6_out);
endmodule
