// Logisim project Project 3 (CD4511).circ as structural Verilog: 1 circuit, main circuit cd4511
module cd4511 (
  input  D1,
  input  D2,
  input  D3,
  input  D0,
  output f,
  output g,
  output a,
  output b,
  output c,
  output d,
  output e
);

  wire n7447_1_pin3;

  _7447 #(.ShowInternalStructure("true")) u_7447_1 (
    .pin1(D1), .pin2(D2), .pin3(n7447_1_pin3), .pin4(n7447_1_pin3), .pin5(n7447_1_pin3), .pin6(D3),
    .pin7(D0), .pin15(f), .pin14(g), .pin13(a), .pin12(b), .pin11(c), .pin10(d), .pin9(e));
  // also tied to VCC on the sheet: n7447_1_pin3
endmodule
