// Logisim project Project 3 (CD4518).circ as structural Verilog: 1 circuit, main circuit cd4518
module cd4518 (
  input  A_RESET,
  input  A_ENABLE,
  input  A_CLOCK,
  input  B_RESET,
  input  B_ENABLE,
  input  B_CLOCK,
  output A1,
  output A2,
  output A3,
  output A4,
  output B1,
  output B2,
  output B3,
  output B4
);

  wire and_1_out, and_2_out, and_3_out, and_4_out, and_5_out, and_6_out, and_7_out, and_8_out, d_ff_1_q,
       d_ff_1_qn, d_ff_2_q, d_ff_2_qn, d_ff_3_q, d_ff_3_qn, d_ff_4_q, d_ff_4_qn, d_ff_5_q, d_ff_5_qn,
       d_ff_6_q, d_ff_6_qn, d_ff_7_q, d_ff_7_qn, d_ff_8_q, d_ff_8_qn, nand_1_out, nand_2_out, nor_1_out,
       nor_2_out, not_1_out, not_2_out, not_3_out, not_4_out, not_5_out, not_6_out, not_7_out, not_8_out,
       not_10_out, not_12_out, not_14_out, not_16_out, not_18_out, not_20_out, not_22_out, not_23_out,
       not_25_out, not_26_out;

  not not_1 (not_1_out, A_RESET);
  not not_2 (not_2_out, A_CLOCK);
  not not_3 (not_3_out, B_RESET);
  not not_4 (not_4_out, B_CLOCK);
  not not_5 (not_5_out, not_1_out);
  not not_6 (not_6_out, nand_1_out);
  nand nand_1 (nand_1_out, A_ENABLE, not_2_out);
  D_Flip_Flop #(.trigger("falling")) d_ff_1 (
    .D(d_ff_1_qn), .clk(not_8_out), .Q(d_ff_1_q), .Qn(d_ff_1_qn), .reset(not_7_out));  // open: preset
  not not_7 (not_7_out, not_3_out);
  not not_8 (not_8_out, nand_2_out);
  nand nand_2 (nand_2_out, B_ENABLE, not_4_out);
  not not_9 (A1, not_10_out);
  not not_10 (not_10_out, d_ff_2_q);
  D_Flip_Flop #(.trigger("falling")) d_ff_2 (
    .D(d_ff_2_qn), .clk(not_6_out), .Q(d_ff_2_q), .Qn(d_ff_2_qn), .reset(not_5_out));  // open: preset
  not not_11 (B1, not_12_out);
  not not_12 (not_12_out, d_ff_1_q);
  and and_1 (and_1_out, ~nand_1_out, ~not_10_out, ~not_23_out);  // AND_Gate
  and and_2 (and_2_out, ~nand_2_out, ~not_12_out, ~not_26_out);  // AND_Gate
  not not_13 (A2, not_14_out);
  not not_14 (not_14_out, d_ff_3_q);
  D_Flip_Flop #(.trigger("falling")) d_ff_3 (
    .D(d_ff_3_qn), .clk(and_1_out), .Q(d_ff_3_q), .Qn(d_ff_3_qn), .reset(not_5_out));  // open: preset
  not not_15 (B2, not_16_out);
  not not_16 (not_16_out, d_ff_4_q);
  D_Flip_Flop #(.trigger("falling")) d_ff_4 (
    .D(d_ff_4_qn), .clk(and_2_out), .Q(d_ff_4_q), .Qn(d_ff_4_qn), .reset(not_7_out));  // open: preset
  and and_3 (and_3_out, ~nand_2_out, ~not_12_out, ~d_ff_4_qn);  // AND_Gate
  D_Flip_Flop #(.trigger("falling")) d_ff_5 (
    .D(d_ff_5_qn), .clk(and_4_out), .Q(d_ff_5_q), .Qn(d_ff_5_qn), .reset(not_5_out));  // open: preset
  and and_4 (and_4_out, ~nand_1_out, ~not_10_out, ~d_ff_3_qn);  // AND_Gate
  not not_17 (B3, not_18_out);
  not not_18 (not_18_out, d_ff_6_q);
  D_Flip_Flop #(.trigger("falling")) d_ff_6 (
    .D(d_ff_6_qn), .clk(and_3_out), .Q(d_ff_6_q), .Qn(d_ff_6_qn), .reset(not_7_out));  // open: preset
  not not_19 (A3, not_20_out);
  not not_20 (not_20_out, d_ff_5_q);
  and and_5 (and_5_out, ~d_ff_5_qn, ~d_ff_3_qn);  // AND_Gate
  and and_6 (and_6_out, ~d_ff_6_qn, ~d_ff_4_qn);  // AND_Gate
  D_Flip_Flop #(.trigger("falling")) d_ff_7 (
    .D(d_ff_7_qn), .clk(and_7_out), .Q(d_ff_7_q), .Qn(d_ff_7_qn), .reset(not_5_out));  // open: preset
  and and_7 (and_7_out, ~nand_1_out, ~not_10_out, ~nor_1_out);  // AND_Gate
  nor nor_1 (nor_1_out, and_5_out, not_23_out);
  D_Flip_Flop #(.trigger("falling")) d_ff_8 (
    .D(d_ff_8_qn), .clk(and_8_out), .Q(d_ff_8_q), .Qn(d_ff_8_qn), .reset(not_7_out));  // open: preset
  and and_8 (and_8_out, ~nand_2_out, ~not_12_out, ~nor_2_out);  // AND_Gate
  nor nor_2 (nor_2_out, and_6_out, not_26_out);
  not not_21 (A4, not_22_out);
  not not_22 (not_22_out, d_ff_7_q);
  not not_23 (not_23_out, d_ff_7_qn);
  not not_24 (B4, not_25_out);
  not not_25 (not_25_out, d_ff_8_q);
  not not_26 (not_26_out, d_ff_8_qn);
endmodule
