// Logisim project Project 3 (Initial Simulation).circ as structural Verilog: 5 circuits, main circuit copy_main
module main (
  input  R1,
  input  SW,
  input  PSW,
  input  R2
);

  wire A, A1, and_1_out, and_2_out, and_3_out, and_4_out, and_5_out, and_6_out, and_7_out, and_8_out,
       and_9_out, and_10_out, and_11_out, and_12_out, and_13_out, and_14_out, and_15_out, and_16_out, B, B1,
       C, C1, cd4511_1_a, cd4511_1_b, cd4511_1_c, cd4511_1_d, cd4511_1_e, cd4511_1_f, cd4511_1_g, cd4511_2_a,
       cd4511_2_b, cd4511_2_c, cd4511_2_d, cd4511_2_e, cd4511_2_f, cd4511_2_g, cd4511_3_a, cd4511_3_b,
       cd4511_3_c, cd4511_3_d, cd4511_3_e, cd4511_3_f, cd4511_3_g, cd4511_4_a, cd4511_4_b, cd4511_4_c,
       cd4511_4_d, cd4511_4_e, cd4511_4_f, cd4511_4_g, cd4511_5_a, cd4511_5_b, cd4511_5_c, cd4511_5_d,
       cd4511_5_e, cd4511_5_f, cd4511_5_g, cd4511_6_a, cd4511_6_b, cd4511_6_c, cd4511_6_d, cd4511_6_e,
       cd4511_6_f, cd4511_6_g, cd4518_1_a1, cd4518_1_a2, cd4518_1_a3, cd4518_1_a4, cd4518_1_b1, cd4518_1_b2,
       cd4518_1_b3, cd4518_1_b4, cd4518_4_a1, cd4518_4_a2, cd4518_4_a3, cd4518_4_a4, cd4518_4_b1,
       cd4518_4_b2, cd4518_4_b3, cd4518_4_b4, cd4518_5_a1, cd4518_5_a2, cd4518_5_a3, cd4518_5_a4,
       cd4518_5_b1, cd4518_5_b2, cd4518_5_b3, cd4518_5_b4, clock_1_out, cmos_74hc157_1_y1, cmos_74hc157_1_y2,
       cmos_74hc157_1_y3, cmos_74hc157_1_y4, D, D1, d_ff_1_q, d_ff_2_q, d_ff_3_q, d_ff_4_q, d_ff_5_q, E, E1,
       F, F1, G, G1, H, H1, multiplexer_1_out, multiplexer_2_out, multiplexer_3_out, multiplexer_4_out,
       multiplexer_5_out, multiplexer_6_out, multiplexer_7_out, multiplexer_8_out, multiplexer_9_out,
       multiplexer_10_out, multiplexer_11_out, multiplexer_12_out, nor_1_out, nor_2_out, nor_3_out,
       nor_4_out, nor_5_out, not_1_out, not_2_out, or_1_out, or_2_out, or_3_out, or_4_out, or_5_out, or_6_out;

  or or_1 (or_1_out, and_1_out, R1);
  and and_1 (and_1_out, cd4518_1_b2, 1'b1, cd4518_1_a3);
  _7_Segment_Display #(.active("false"), .decimalPoint("false")) u_7_segment_display_1 (
    .g(cd4511_1_g), .f(cd4511_1_f), .a(cd4511_1_a), .b(cd4511_1_b), .e(cd4511_1_e), .d(cd4511_1_d),
    .c(cd4511_1_c));
  cd4511 cd4511_1 (
    .D1(cd4518_1_b2), .D2(cd4518_1_b3), .D3(cd4518_1_b4), .D0(cd4518_1_b1), .f(cd4511_1_f), .g(cd4511_1_g),
    .a(cd4511_1_a), .b(cd4511_1_b), .c(cd4511_1_c), .d(cd4511_1_d), .e(cd4511_1_e));
  cd4518 cd4518_1 (
    .B_CLOCK(and_2_out), .B_RESET(or_1_out), .B_ENABLE(1'b1), .A_RESET(or_1_out), .A_ENABLE(1'b1),
    .A_CLOCK(and_3_out), .B1(cd4518_1_b1), .A1(cd4518_1_a1), .B2(cd4518_1_b2), .A2(cd4518_1_a2),
    .B3(cd4518_1_b3), .A3(cd4518_1_a3), .B4(cd4518_1_b4), .A4(cd4518_1_a4));
  D_Flip_Flop d_ff_1 (.D(1'b1), .clk(cd4518_1_a2), .Q(d_ff_1_q), .reset(or_1_out));  // open: Qn, preset
  or or_2 (or_2_out, not_1_out, R2);
  _7_Segment_Display #(.active("false"), .decimalPoint("false")) u_7_segment_display_2 (
    .g(cd4511_2_g), .f(cd4511_2_f), .a(cd4511_2_a), .b(cd4511_2_b), .e(cd4511_2_e), .d(cd4511_2_d),
    .c(cd4511_2_c));
  cd4511 cd4511_2 (
    .D1(cd4518_1_a2), .D2(cd4518_1_a3), .D3(cd4518_1_a4), .D0(cd4518_1_a1), .f(cd4511_2_f), .g(cd4511_2_g),
    .a(cd4511_2_a), .b(cd4511_2_b), .c(cd4511_2_c), .d(cd4511_2_d), .e(cd4511_2_e));
  nor nor_1 (nor_1_out, cd4518_1_a2, cd4518_1_a3, cd4518_1_a4, cd4518_1_a1);
  and and_2 (and_2_out, nor_1_out, d_ff_1_q);
  Multiplexer multiplexer_1 (.in0(E1), .in1(E), .out(multiplexer_1_out), .sel(SW));
  Multiplexer multiplexer_2 (.in0(D1), .in1(D), .out(multiplexer_2_out));  // open: sel
  Multiplexer multiplexer_3 (.in0(G1), .in1(G), .out(multiplexer_3_out));  // open: sel
  _7_Segment_Display #(.active("false"), .decimalPoint("false")) u_7_segment_display_3 (
    .g(cd4511_3_g), .f(cd4511_3_f), .a(cd4511_3_a), .b(cd4511_3_b), .e(cd4511_3_e), .d(cd4511_3_d),
    .c(cd4511_3_c));
  cd4511 cd4511_3 (
    .D1(multiplexer_4_out), .D2(multiplexer_1_out), .D3(multiplexer_3_out), .D0(multiplexer_5_out),
    .f(cd4511_3_f), .g(cd4511_3_g), .a(cd4511_3_a), .b(cd4511_3_b), .c(cd4511_3_c), .d(cd4511_3_d),
    .e(cd4511_3_e));
  Multiplexer multiplexer_4 (.in0(F1), .in1(F), .out(multiplexer_4_out), .sel(SW));
  and and_3 (and_3_out, F1, E1);
  or or_3 (or_3_out, or_1_out, and_3_out);
  cd4518 cd4518_2 (
    .B_CLOCK(and_7_out), .B_RESET(or_3_out), .B_ENABLE(1'b1), .A_RESET(or_1_out), .A_ENABLE(1'b1),
    .A_CLOCK(and_9_out), .B1(H1), .A1(D1), .B2(F1), .A2(A1), .B3(E1), .A3(B1), .B4(G1), .A4(C1));
  Multiplexer multiplexer_5 (.in0(H1), .in1(H), .out(multiplexer_5_out), .sel(SW));
  Multiplexer multiplexer_6 (.in0(C1), .in1(C), .out(multiplexer_6_out));  // open: sel
  and and_4 (and_4_out, F, E);
  or or_4 (or_4_out, or_2_out, and_4_out);
  cd4518 cd4518_3 (
    .B_CLOCK(and_8_out), .B_RESET(or_4_out), .B_ENABLE(1'b1), .A_RESET(or_2_out), .A_ENABLE(1'b1),
    .A_CLOCK(and_10_out), .B1(H), .A1(D), .B2(F), .A2(A), .B3(E), .A3(B), .B4(G), .A4(C));
  nor nor_2 (nor_2_out, D1, A1, B1, C1);
  Multiplexer multiplexer_7 (.in0(B1), .in1(B), .out(multiplexer_7_out));  // open: sel
  nor nor_3 (nor_3_out, D, A, B, C);
  D_Flip_Flop d_ff_2 (.D(1'b1), .clk(and_5_out), .Q(d_ff_2_q), .reset(or_1_out));  // open: Qn, preset
  and and_5 (and_5_out, D1, C1);
  D_Flip_Flop d_ff_3 (.D(1'b1), .clk(and_6_out), .Q(d_ff_3_q), .reset(or_2_out));  // open: Qn, preset
  and and_6 (and_6_out, D, C);
  _7_Segment_Display #(.active("false"), .decimalPoint("false")) u_7_segment_display_4 (
    .g(cd4511_4_g), .f(cd4511_4_f), .a(cd4511_4_a), .b(cd4511_4_b), .e(cd4511_4_e), .d(cd4511_4_d),
    .c(cd4511_4_c));
  cd4511 cd4511_4 (
    .D1(multiplexer_8_out), .D2(multiplexer_7_out), .D3(multiplexer_6_out), .D0(multiplexer_2_out),
    .f(cd4511_4_f), .g(cd4511_4_g), .a(cd4511_4_a), .b(cd4511_4_b), .c(cd4511_4_c), .d(cd4511_4_d),
    .e(cd4511_4_e));
  Multiplexer multiplexer_8 (.in0(A1), .in1(A), .out(multiplexer_8_out));  // open: sel
  Multiplexer multiplexer_9 (.in0(cd4518_4_b2), .in1(cd4518_5_b2), .out(multiplexer_9_out));  // open: sel
  and and_7 (and_7_out, nor_2_out, d_ff_2_q);
  and and_8 (and_8_out, nor_3_out, d_ff_3_q);
  Multiplexer multiplexer_10 (.in0(cd4518_4_b3), .in1(cd4518_5_b3), .out(multiplexer_10_out));  // open: sel
  _7_Segment_Display #(.active("false"), .decimalPoint("false")) u_7_segment_display_5 (
    .g(cd4511_5_g), .f(cd4511_5_f), .a(cd4511_5_a), .b(cd4511_5_b), .e(cd4511_5_e), .d(cd4511_5_d),
    .c(cd4511_5_c));
  cd4511 cd4511_5 (
    .D1(multiplexer_9_out), .D2(multiplexer_10_out), .D3(multiplexer_11_out), .D0(multiplexer_12_out),
    .f(cd4511_5_f), .g(cd4511_5_g), .a(cd4511_5_a), .b(cd4511_5_b), .c(cd4511_5_c), .d(cd4511_5_d),
    .e(cd4511_5_e));
  Multiplexer multiplexer_11 (.in0(cd4518_4_b4), .in1(cd4518_5_b4), .out(multiplexer_11_out));  // open: sel
  Multiplexer multiplexer_12 (.in0(cd4518_4_b1), .in1(cd4518_5_b1), .out(multiplexer_12_out));  // open: sel
  and and_9 (and_9_out, cd4518_4_b3, cd4518_4_b2);
  or or_5 (or_5_out, or_1_out, and_9_out);
  cd4518 cd4518_4 (
    .B_CLOCK(and_13_out), .B_RESET(or_5_out), .B_ENABLE(1'b1), .A_RESET(or_1_out), .A_ENABLE(1'b1),
    .A_CLOCK(clock_1_out), .B1(cd4518_4_b1), .A1(cd4518_4_a1), .B2(cd4518_4_b2), .A2(cd4518_4_a2),
    .B3(cd4518_4_b3), .A3(cd4518_4_a3), .B4(cd4518_4_b4), .A4(cd4518_4_a4));
  nor nor_4 (nor_4_out, cd4518_4_a1, cd4518_4_a2, cd4518_4_a3, cd4518_4_a4);
  and and_10 (and_10_out, cd4518_5_b3, cd4518_5_b2);
  or or_6 (or_6_out, or_2_out, and_10_out);
  cd4518 cd4518_5 (
    .B_CLOCK(and_14_out), .B_RESET(or_6_out), .B_ENABLE(1'b1), .A_RESET(or_2_out), .A_ENABLE(1'b1),
    .A_CLOCK(and_15_out), .B1(cd4518_5_b1), .A1(cd4518_5_a1), .B2(cd4518_5_b2), .A2(cd4518_5_a2),
    .B3(cd4518_5_b3), .A3(cd4518_5_a3), .B4(cd4518_5_b4), .A4(cd4518_5_a4));
  D_Flip_Flop d_ff_4 (.D(1'b1), .clk(and_11_out), .Q(d_ff_4_q), .reset(or_1_out));  // open: Qn, preset
  and and_11 (and_11_out, cd4518_4_a1, cd4518_4_a4);
  D_Flip_Flop d_ff_5 (.D(1'b1), .clk(and_12_out), .Q(d_ff_5_q), .reset(or_2_out));  // open: Qn, preset
  and and_12 (and_12_out, cd4518_5_a1, cd4518_5_a4);
  nor nor_5 (nor_5_out, cd4518_5_a1, cd4518_5_a2, cd4518_5_a3, cd4518_5_a4);
  and and_13 (and_13_out, nor_4_out, d_ff_4_q);
  _7_Segment_Display #(.active("false"), .decimalPoint("false")) u_7_segment_display_6 (
    .g(cd4511_6_g), .f(cd4511_6_f), .a(cd4511_6_a), .b(cd4511_6_b), .e(cd4511_6_e), .d(cd4511_6_d),
    .c(cd4511_6_c));
  cd4511 cd4511_6 (
    .D1(cmos_74hc157_1_y3), .D2(cmos_74hc157_1_y4), .D3(cmos_74hc157_1_y2), .D0(cmos_74hc157_1_y1),
    .f(cd4511_6_f), .g(cd4511_6_g), .a(cd4511_6_a), .b(cd4511_6_b), .c(cd4511_6_c), .d(cd4511_6_d),
    .e(cd4511_6_e));
  and and_14 (and_14_out, nor_5_out, d_ff_5_q);
  cmos_74HC157 cmos_74hc157_1 (
    .S(SW), .E(1'b0), .A1(cd4518_5_a1), .A0(cd4518_4_a1), .B1(cd4518_5_a4), .B0(cd4518_4_a4),
    .C1(cd4518_5_a2), .C0(cd4518_4_a2), .D1(cd4518_5_a3), .D0(cd4518_4_a3), .Y1(cmos_74hc157_1_y1),
    .Y2(cmos_74hc157_1_y2), .Y3(cmos_74hc157_1_y3), .Y4(cmos_74hc157_1_y4));
  not not_1 (not_1_out, SW);
  and and_15 (and_15_out, and_16_out, not_2_out);
  and and_16 (and_16_out, SW, clock_1_out);
  not not_2 (not_2_out, PSW);
  Clock clock_1 (.out(clock_1_out));
endmodule

module cd4518 (
  input  A_RESET,
  input  A_ENABLE,
  input  A_CLOCK,
  input  B_RESET,
  input  B_ENABLE,
  input  B_CLOCK,
  output A1,
  output A2,
  output A3,
  output A4,
  output B1,
  output B2,
  output B3,
  output B4
);

  wire and_1_out, and_2_out, and_3_out, and_4_out, and_5_out, and_6_out, and_7_out, and_8_out, d_ff_1_q,
       d_ff_1_qn, d_ff_2_q, d_ff_2_qn, d_ff_3_q, d_ff_3_qn, d_ff_4_q, d_ff_4_qn, d_ff_5_q, d_ff_5_qn,
       d_ff_6_q, d_ff_6_qn, d_ff_7_q, d_ff_7_qn, d_ff_8_q, d_ff_8_qn, nand_1_out, nand_2_out, nor_1_out,
       nor_2_out, not_1_out, not_2_out, not_3_out, not_4_out, not_5_out, not_6_out, not_7_out, not_8_out,
       not_10_out, not_12_out, not_14_out, not_16_out, not_18_out, not_20_out, not_22_out, not_23_out,
       not_25_out, not_26_out;

  not not_1 (not_1_out, A_RESET);
  not not_2 (not_2_out, A_CLOCK);
  not not_3 (not_3_out, B_RESET);
  not not_4 (not_4_out, B_CLOCK);
  not not_5 (not_5_out, not_1_out);
  not not_6 (not_6_out, nand_1_out);
  nand nand_1 (nand_1_out, A_ENABLE, not_2_out);
  D_Flip_Flop #(.trigger("falling")) d_ff_1 (
    .D(d_ff_1_qn), .clk(not_8_out), .Q(d_ff_1_q), .Qn(d_ff_1_qn), .reset(not_7_out));  // open: preset
  not not_7 (not_7_out, not_3_out);
  not not_8 (not_8_out, nand_2_out);
  nand nand_2 (nand_2_out, B_ENABLE, not_4_out);
  not not_9 (A1, not_10_out);
  not not_10 (not_10_out, d_ff_2_q);
  D_Flip_Flop #(.trigger("falling")) d_ff_2 (
    .D(d_ff_2_qn), .clk(not_6_out), .Q(d_ff_2_q), .Qn(d_ff_2_qn), .reset(not_5_out));  // open: preset
  not not_11 (B1, not_12_out);
  not not_12 (not_12_out, d_ff_1_q);
  and and_1 (and_1_out, ~nand_1_out, ~not_10_out, ~not_23_out);  // AND_Gate
  and and_2 (and_2_out, ~nand_2_out, ~not_12_out, ~not_26_out);  // AND_Gate
  not not_13 (A2, not_14_out);
  not not_14 (not_14_out, d_ff_3_q);
  D_Flip_Flop #(.trigger("falling")) d_ff_3 (
    .D(d_ff_3_qn), .clk(and_1_out), .Q(d_ff_3_q), .Qn(d_ff_3_qn), .reset(not_5_out));  // open: preset
  not not_15 (B2, not_16_out);
  not not_16 (not_16_out, d_ff_4_q);
  D_Flip_Flop #(.trigger("falling")) d_ff_4 (
    .D(d_ff_4_qn), .clk(and_2_out), .Q(d_ff_4_q), .Qn(d_ff_4_qn), .reset(not_7_out));  // open: preset
  and and_3 (and_3_out, ~nand_2_out, ~not_12_out, ~d_ff_4_qn);  // AND_Gate
  D_Flip_Flop #(.trigger("falling")) d_ff_5 (
    .D(d_ff_5_qn), .clk(and_4_out), .Q(d_ff_5_q), .Qn(d_ff_5_qn), .reset(not_5_out));  // open: preset
  and and_4 (and_4_out, ~nand_1_out, ~not_10_out, ~d_ff_3_qn);  // AND_Gate
  not not_17 (B3, not_18_out);
  not not_18 (not_18_out, d_ff_6_q);
  D_Flip_Flop #(.trigger("falling")) d_ff_6 (
    .D(d_ff_6_qn), .clk(and_3_out), .Q(d_ff_6_q), .Qn(d_ff_6_qn), .reset(not_7_out));  // open: preset
  not not_19 (A3, not_20_out);
  not not_20 (not_20_out, d_ff_5_q);
  and and_5 (and_5_out, ~d_ff_5_qn, ~d_ff_3_qn);  // AND_Gate
  and and_6 (and_6_out, ~d_ff_6_qn, ~d_ff_4_qn);  // AND_Gate
  D_Flip_Flop #(.trigger("falling")) d_ff_7 (
    .D(d_ff_7_qn), .clk(and_7_out), .Q(d_ff_7_q), .Qn(d_ff_7_qn), .reset(not_5_out));  // open: preset
  and and_7 (and_7_out, ~nand_1_out, ~not_10_out, ~nor_1_out);  // AND_Gate
  nor nor_1 (nor_1_out, and_5_out, not_23_out);
  D_Flip_Flop #(.trigger("falling")) d_ff_8 (
    .D(d_ff_8_qn), .clk(and_8_out), .Q(d_ff_8_q), .Qn(d_ff_8_qn), .reset(not_7_out));  // open: preset
  and and_8 (and_8_out, ~nand_2_out, ~not_12_out, ~nor_2_out);  // AND_Gate
  nor nor_2 (nor_2_out, and_6_out, not_26_out);
  not not_21 (A4, not_22_out);
  not not_22 (not_22_out, d_ff_7_q);
  not not_23 (not_23_out, d_ff_7_qn);
  not not_24 (B4, not_25_out);
  not not_25 (not_25_out, d_ff_8_q);
  not not_26 (not_26_out, d_ff_8_qn);
endmodule

module cd4511 (
  input  D1,
  input  D2,
  input  D3,
  input  D0,
  output f,
  output g,
  output a,
  output b,
  output c,
  output d,
  output e
);

  wire n7447_1_pin3;

  _7447 #(.ShowInternalStructure("true")) u_7447_1 (
    .pin1(D1), .pin2(D2), .pin3(n7447_1_pin3), .pin4(n7447_1_pin3), .pin5(n7447_1_pin3), .pin6(D3),
    .pin7(D0), .pin15(f), .pin14(g), .pin13(a), .pin12(b), .pin11(c), .pin10(d), .pin9(e));
  // also tied to VCC on the sheet: n7447_1_pin3
endmodule

module cmos_74HC157 (
  input  S,
  input  E,
  input  A1,
  input  A0,
  input  B1,
  input  B0,
  input  C1,
  input  C0,
  input  D1,
  input  D0,
  output Y1,
  output Y2,
  output Y3,
  output Y4
);

  wire and_1_out, and_2_out, and_3_out, and_4_out, and_5_out, and_6_out, and_7_out, and_8_out, buffer_1_out,
       buffer_2_out, buffer_3_out, buffer_4_out, buffer_5_out, buffer_6_out, buffer_7_out, buffer_8_out,
       buffer_9_out, buffer_10_out, nor_1_out, nor_2_out, nor_3_out, nor_4_out, nor_5_out, nor_6_out,
       not_1_out;

  buf buffer_1 (buffer_1_out, S);
  buf buffer_2 (buffer_2_out, E);
  buf buffer_3 (buffer_3_out, A1);
  buf buffer_4 (buffer_4_out, A0);
  buf buffer_5 (buffer_5_out, B1);
  buf buffer_6 (buffer_6_out, B0);
  buf buffer_7 (buffer_7_out, C1);
  buf buffer_8 (buffer_8_out, C0);
  buf buffer_9 (buffer_9_out, D1);
  buf buffer_10 (buffer_10_out, D0);
  not not_1 (not_1_out, buffer_1_out);
  nor nor_1 (nor_1_out, not_1_out, buffer_2_out);
  nor nor_2 (nor_2_out, buffer_1_out, buffer_2_out);
  and and_1 (and_1_out, nor_1_out, buffer_3_out);
  and and_2 (and_2_out, nor_2_out, buffer_4_out);
  and and_3 (and_3_out, nor_1_out, buffer_5_out);
  and and_4 (and_4_out, nor_2_out, buffer_6_out);
  and and_5 (and_5_out, nor_1_out, buffer_7_out);
  and and_6 (and_6_out, nor_2_out, buffer_8_out);
  and and_7 (and_7_out, nor_1_out, buffer_9_out);
  and and_8 (and_8_out, nor_2_out, buffer_10_out);
  nor nor_3 (nor_3_out, and_1_out, and_2_out);
  not not_2 (Y1, nor_3_out);
  nor nor_4 (nor_4_out, and_3_out, and_4_out);
  not not_3 (Y2, nor_4_out);
  nor nor_5 (nor_5_out, and_5_out, and_6_out);
  not not_4 (Y3, nor_5_out);
  nor nor_6 (nor_6_out, and_7_out, and_8_out);
  not not_5 (Y4, nor_6_out);
endmodule

module copy_main (
  input  R1,
  input  SW,
  input  PSW,
  input  R2
);

  wire A, A1, and_1_out, and_2_out, and_3_out, and_4_out, and_5_out, and_6_out, and_7_out, B, B1, C, C1,
       cd4511_1_a, cd4511_1_b, cd4511_1_c, cd4511_1_d, cd4511_1_e, cd4511_1_f, cd4511_1_g, cd4511_2_a,
       cd4511_2_b, cd4511_2_c, cd4511_2_d, cd4511_2_e, cd4511_2_f, cd4511_2_g, cd4511_3_a, cd4511_3_b,
       cd4511_3_c, cd4511_3_d, cd4511_3_e, cd4511_3_f, cd4511_3_g, cd4511_4_a, cd4511_4_b, cd4511_4_c,
       cd4511_4_d, cd4511_4_e, cd4511_4_f, cd4511_4_g, cd4511_5_a, cd4511_5_b, cd4511_5_c, cd4511_5_d,
       cd4511_5_e, cd4511_5_f, cd4511_5_g, cd4511_6_a, cd4511_6_b, cd4511_6_c, cd4511_6_d, cd4511_6_e,
       cd4511_6_f, cd4511_6_g, cd4518_1_a1, cd4518_1_a2, cd4518_1_a3, cd4518_1_a4, cd4518_1_b1, cd4518_1_b2,
       cd4518_1_b3, cd4518_1_b4, cd4518_4_a1, cd4518_4_a2, cd4518_4_a3, cd4518_4_a4, cd4518_4_b1,
       cd4518_4_b2, cd4518_4_b3, cd4518_4_b4, cd4518_5_a1, cd4518_5_a2, cd4518_5_a3, cd4518_5_a4,
       cd4518_5_b1, cd4518_5_b2, cd4518_5_b3, cd4518_5_b4, clock_1_out, cmos_74hc157_1_y1, cmos_74hc157_1_y2,
       cmos_74hc157_1_y3, cmos_74hc157_1_y4, D, D1, E, E1, F, F1, G, G1, H, H1, multiplexer_1_out,
       multiplexer_2_out, multiplexer_3_out, multiplexer_4_out, multiplexer_5_out, multiplexer_6_out,
       multiplexer_7_out, multiplexer_8_out, multiplexer_9_out, multiplexer_10_out, multiplexer_11_out,
       multiplexer_12_out, nor_1_out, nor_2_out, nor_3_out, nor_4_out, nor_5_out, not_1_out, or_1_out,
       or_2_out, or_3_out, or_4_out, or_5_out, or_6_out, or_7_out;

  or or_1 (or_1_out, and_1_out, R1);
  and and_1 (and_1_out, cd4518_1_b2, cd4518_1_a3);
  _7_Segment_Display #(.active("false"), .decimalPoint("false")) u_7_segment_display_1 (
    .g(cd4511_1_g), .f(cd4511_1_f), .a(cd4511_1_a), .b(cd4511_1_b), .e(cd4511_1_e), .d(cd4511_1_d),
    .c(cd4511_1_c));
  cd4511 cd4511_1 (
    .D1(cd4518_1_b2), .D2(cd4518_1_b3), .D3(cd4518_1_b4), .D0(cd4518_1_b1), .f(cd4511_1_f), .g(cd4511_1_g),
    .a(cd4511_1_a), .b(cd4511_1_b), .c(cd4511_1_c), .d(cd4511_1_d), .e(cd4511_1_e));
  or or_2 (or_2_out, and_1_out, or_1_out);
  cd4518 cd4518_1 (
    .B_CLOCK(nor_1_out), .B_RESET(or_2_out), .B_ENABLE(1'b1), .A_RESET(or_1_out), .A_ENABLE(1'b1),
    .A_CLOCK(and_2_out), .B1(cd4518_1_b1), .A1(cd4518_1_a1), .B2(cd4518_1_b2), .A2(cd4518_1_a2),
    .B3(cd4518_1_b3), .A3(cd4518_1_a3), .B4(cd4518_1_b4), .A4(cd4518_1_a4));
  or or_3 (or_3_out, not_1_out, R2);
  _7_Segment_Display #(.active("false"), .decimalPoint("false")) u_7_segment_display_2 (
    .g(cd4511_2_g), .f(cd4511_2_f), .a(cd4511_2_a), .b(cd4511_2_b), .e(cd4511_2_e), .d(cd4511_2_d),
    .c(cd4511_2_c));
  cd4511 cd4511_2 (
    .D1(cd4518_1_a2), .D2(cd4518_1_a3), .D3(cd4518_1_a4), .D0(cd4518_1_a1), .f(cd4511_2_f), .g(cd4511_2_g),
    .a(cd4511_2_a), .b(cd4511_2_b), .c(cd4511_2_c), .d(cd4511_2_d), .e(cd4511_2_e));
  nor nor_1 (nor_1_out, cd4518_1_a2, cd4518_1_a3, cd4518_1_a4, cd4518_1_a1);
  Multiplexer multiplexer_1 (.in0(E1), .in1(E), .out(multiplexer_1_out), .sel(SW));
  Multiplexer multiplexer_2 (.in0(D1), .in1(D), .out(multiplexer_2_out));  // open: sel
  Multiplexer multiplexer_3 (.in0(G1), .in1(G), .out(multiplexer_3_out));  // open: sel
  _7_Segment_Display #(.active("false"), .decimalPoint("false")) u_7_segment_display_3 (
    .g(cd4511_3_g), .f(cd4511_3_f), .a(cd4511_3_a), .b(cd4511_3_b), .e(cd4511_3_e), .d(cd4511_3_d),
    .c(cd4511_3_c));
  cd4511 cd4511_3 (
    .D1(multiplexer_4_out), .D2(multiplexer_1_out), .D3(multiplexer_3_out), .D0(multiplexer_5_out),
    .f(cd4511_3_f), .g(cd4511_3_g), .a(cd4511_3_a), .b(cd4511_3_b), .c(cd4511_3_c), .d(cd4511_3_d),
    .e(cd4511_3_e));
  Multiplexer multiplexer_4 (.in0(F1), .in1(F), .out(multiplexer_4_out), .sel(SW));
  and and_2 (and_2_out, F1, E1);
  or or_4 (or_4_out, or_1_out, and_2_out);
  cd4518 cd4518_2 (
    .B_CLOCK(nor_2_out), .B_RESET(or_4_out), .B_ENABLE(1'b1), .A_RESET(or_1_out), .A_ENABLE(1'b1),
    .A_CLOCK(and_4_out), .B1(H1), .A1(D1), .B2(F1), .A2(A1), .B3(E1), .A3(B1), .B4(G1), .A4(C1));
  Multiplexer multiplexer_5 (.in0(H1), .in1(H), .out(multiplexer_5_out), .sel(SW));
  Multiplexer multiplexer_6 (.in0(C1), .in1(C), .out(multiplexer_6_out));  // open: sel
  and and_3 (and_3_out, F, E);
  or or_5 (or_5_out, or_3_out, and_3_out);
  cd4518 cd4518_3 (
    .B_CLOCK(nor_3_out), .B_RESET(or_5_out), .B_ENABLE(1'b1), .A_RESET(or_3_out), .A_ENABLE(1'b1),
    .A_CLOCK(and_5_out), .B1(H), .A1(D), .B2(F), .A2(A), .B3(E), .A3(B), .B4(G), .A4(C));
  nor nor_2 (nor_2_out, D1, A1, B1, C1);
  Multiplexer multiplexer_7 (.in0(B1), .in1(B), .out(multiplexer_7_out));  // open: sel
  nor nor_3 (nor_3_out, D, A, B, C);
  _7_Segment_Display #(.active("false"), .decimalPoint("false")) u_7_segment_display_4 (
    .g(cd4511_4_g), .f(cd4511_4_f), .a(cd4511_4_a), .b(cd4511_4_b), .e(cd4511_4_e), .d(cd4511_4_d),
    .c(cd4511_4_c));
  cd4511 cd4511_4 (
    .D1(multiplexer_8_out), .D2(multiplexer_7_out), .D3(multiplexer_6_out), .D0(multiplexer_2_out),
    .f(cd4511_4_f), .g(cd4511_4_g), .a(cd4511_4_a), .b(cd4511_4_b), .c(cd4511_4_c), .d(cd4511_4_d),
    .e(cd4511_4_e));
  Multiplexer multiplexer_8 (.in0(A1), .in1(A), .out(multiplexer_8_out));  // open: sel
  Multiplexer multiplexer_9 (.in0(cd4518_4_b2), .in1(cd4518_5_b2), .out(multiplexer_9_out));  // open: sel
  Multiplexer multiplexer_10 (.in0(cd4518_4_b3), .in1(cd4518_5_b3), .out(multiplexer_10_out));  // open: sel
  _7_Segment_Display #(.active("false"), .decimalPoint("false")) u_7_segment_display_5 (
    .g(cd4511_5_g), .f(cd4511_5_f), .a(cd4511_5_a), .b(cd4511_5_b), .e(cd4511_5_e), .d(cd4511_5_d),
    .c(cd4511_5_c));
  cd4511 cd4511_5 (
    .D1(multiplexer_9_out), .D2(multiplexer_10_out), .D3(multiplexer_11_out), .D0(multiplexer_12_out),
    .f(cd4511_5_f), .g(cd4511_5_g), .a(cd4511_5_a), .b(cd4511_5_b), .c(cd4511_5_c), .d(cd4511_5_d),
    .e(cd4511_5_e));
  Multiplexer multiplexer_11 (.in0(cd4518_4_b4), .in1(cd4518_5_b4), .out(multiplexer_11_out));  // open: sel
  Multiplexer multiplexer_12 (.in0(cd4518_4_b1), .in1(cd4518_5_b1), .out(multiplexer_12_out));  // open: sel
  and and_4 (and_4_out, cd4518_4_b3, cd4518_4_b2);
  or or_6 (or_6_out, or_1_out, and_4_out);
  cd4518 cd4518_4 (
    .B_CLOCK(nor_4_out), .B_RESET(or_6_out), .B_ENABLE(1'b1), .A_RESET(or_1_out), .A_ENABLE(1'b1),
    .A_CLOCK(clock_1_out), .B1(cd4518_4_b1), .A1(cd4518_4_a1), .B2(cd4518_4_b2), .A2(cd4518_4_a2),
    .B3(cd4518_4_b3), .A3(cd4518_4_a3), .B4(cd4518_4_b4), .A4(cd4518_4_a4));
  nor nor_4 (nor_4_out, cd4518_4_a1, cd4518_4_a2, cd4518_4_a3, cd4518_4_a4);
  and and_5 (and_5_out, cd4518_5_b3, cd4518_5_b2);
  or or_7 (or_7_out, or_3_out, and_5_out);
  cd4518 cd4518_5 (
    .B_CLOCK(nor_5_out), .B_RESET(or_7_out), .B_ENABLE(1'b1), .A_RESET(or_3_out), .A_ENABLE(1'b1),
    .A_CLOCK(and_6_out), .B1(cd4518_5_b1), .A1(cd4518_5_a1), .B2(cd4518_5_b2), .A2(cd4518_5_a2),
    .B3(cd4518_5_b3), .A3(cd4518_5_a3), .B4(cd4518_5_b4), .A4(cd4518_5_a4));
  nor nor_5 (nor_5_out, cd4518_5_a1, cd4518_5_a2, cd4518_5_a3, cd4518_5_a4);
  _7_Segment_Display #(.active("false"), .decimalPoint("false")) u_7_segment_display_6 (
    .g(cd4511_6_g), .f(cd4511_6_f), .a(cd4511_6_a), .b(cd4511_6_b), .e(cd4511_6_e), .d(cd4511_6_d),
    .c(cd4511_6_c));
  cd4511 cd4511_6 (
    .D1(cmos_74hc157_1_y3), .D2(cmos_74hc157_1_y4), .D3(cmos_74hc157_1_y2), .D0(cmos_74hc157_1_y1),
    .f(cd4511_6_f), .g(cd4511_6_g), .a(cd4511_6_a), .b(cd4511_6_b), .c(cd4511_6_c), .d(cd4511_6_d),
    .e(cd4511_6_e));
  cmos_74HC157 cmos_74hc157_1 (
    .S(SW), .E(1'b0), .A1(cd4518_5_a1), .A0(cd4518_4_a1), .B1(cd4518_5_a4), .B0(cd4518_4_a4),
    .C1(cd4518_5_a2), .C0(cd4518_4_a2), .D1(cd4518_5_a3), .D0(cd4518_4_a3), .Y1(cmos_74hc157_1_y1),
    .Y2(cmos_74hc157_1_y2), .Y3(cmos_74hc157_1_y3), .Y4(cmos_74hc157_1_y4));
  not not_1 (not_1_out, SW);
  and and_6 (and_6_out, and_7_out, PSW);
  and and_7 (and_7_out, SW, clock_1_out);
  Clock clock_1 (.out(clock_1_out));
endmodule
